// Logisim project cpu.circ as structural Verilog: 1 circuit, main circuit cpu
module cpu (
);

  wire [31:0] PC_q;

  Register #(.width(32)) PC (.Q(PC_q));  // open: D, en, clk, clr
  // alu_control_unit alu_control_unit_1: pin names not known
  mem InstMem (.MemAddress(PC_q));  // open: MemWriteMask, MemWriteData, clk, MemReadData
  // control_unit control_unit_1: pin names not known
  // myALU myalu_1: pin names not known
  // regfile RegisterFile: pin names not known
  // mem DataMem: pin names not known
endmodule
